// Digital circuit 16x4bit_mem.dig as structural Verilog
module _16x4bit_mem (
  input  Write,
  input  [3:0] A_In,
  input  [3:0] D_in,
  output [3:0] D_out,
  output [3:0] A_out
);

  wire demultiplexer_1_out_0, demultiplexer_1_out_1, demultiplexer_1_out_2, demultiplexer_1_out_3,
       demultiplexer_1_out_4, demultiplexer_1_out_5, demultiplexer_1_out_6, demultiplexer_1_out_7,
       demultiplexer_1_out_8, demultiplexer_1_out_9, demultiplexer_1_out_10, demultiplexer_1_out_11,
       demultiplexer_1_out_12, demultiplexer_1_out_13, demultiplexer_1_out_14, demultiplexer_1_out_15;
  wire [3:0] M_0_d_out, M_1_d_out, M_2_d_out, M_3_d_out, M_4_d_out, M_5_d_out, M_6_d_out, M_7_d_out,
       M_8_d_out, M_9_d_out, M_10_d_out, M_11_d_out, M_12_d_out, M_13_d_out, M_14_d_out, M_15_d_out;

  Demultiplexer #(.Selector_Bits(4)) demultiplexer_1 (
    .sel(A_In), .in(Write), .out_0(demultiplexer_1_out_0), .out_1(demultiplexer_1_out_1),
    .out_2(demultiplexer_1_out_2), .out_3(demultiplexer_1_out_3), .out_4(demultiplexer_1_out_4),
    .out_5(demultiplexer_1_out_5), .out_6(demultiplexer_1_out_6), .out_7(demultiplexer_1_out_7),
    .out_8(demultiplexer_1_out_8), .out_9(demultiplexer_1_out_9), .out_10(demultiplexer_1_out_10),
    .out_11(demultiplexer_1_out_11), .out_12(demultiplexer_1_out_12), .out_13(demultiplexer_1_out_13),
    .out_14(demultiplexer_1_out_14), .out_15(demultiplexer_1_out_15));
  _4bit_memory M_0 (.D_in(D_in), .Write(demultiplexer_1_out_0), .D_out(M_0_d_out));
  _4bit_memory M_4 (.D_in(D_in), .Write(demultiplexer_1_out_4), .D_out(M_4_d_out));
  _4bit_memory M_8 (.D_in(D_in), .Write(demultiplexer_1_out_8), .D_out(M_8_d_out));
  _4bit_memory M_12 (.D_in(D_in), .Write(demultiplexer_1_out_12), .D_out(M_12_d_out));
  _4bit_memory M_1 (.D_in(D_in), .Write(demultiplexer_1_out_1), .D_out(M_1_d_out));
  _4bit_memory M_5 (.D_in(D_in), .Write(demultiplexer_1_out_5), .D_out(M_5_d_out));
  _4bit_memory M_9 (.D_in(D_in), .Write(demultiplexer_1_out_9), .D_out(M_9_d_out));
  _4bit_memory M_13 (.D_in(D_in), .Write(demultiplexer_1_out_13), .D_out(M_13_d_out));
  _4bit_memory M_2 (.D_in(D_in), .Write(demultiplexer_1_out_2), .D_out(M_2_d_out));
  _4bit_memory M_6 (.D_in(D_in), .Write(demultiplexer_1_out_6), .D_out(M_6_d_out));
  _4bit_memory M_10 (.D_in(D_in), .Write(demultiplexer_1_out_10), .D_out(M_10_d_out));
  _4bit_memory M_14 (.D_in(D_in), .Write(demultiplexer_1_out_14), .D_out(M_14_d_out));
  _4bit_memory M_3 (.D_in(D_in), .Write(demultiplexer_1_out_3), .D_out(M_3_d_out));
  _4bit_memory M_7 (.D_in(D_in), .Write(demultiplexer_1_out_7), .D_out(M_7_d_out));
  _4bit_memory M_11 (.D_in(D_in), .Write(demultiplexer_1_out_11), .D_out(M_11_d_out));
  _4bit_memory M_15 (.D_in(D_in), .Write(demultiplexer_1_out_15), .D_out(M_15_d_out));
  Multiplexer #(.Selector_Bits(4), .Bits(4)) multiplexer_1 (
    .sel(A_In), .in_0(M_0_d_out), .in_1(M_1_d_out), .in_2(M_2_d_out), .in_3(M_3_d_out), .in_4(M_4_d_out),
    .in_5(M_5_d_out), .in_6(M_6_d_out), .in_7(M_7_d_out), .in_8(M_8_d_out), .in_9(M_9_d_out),
    .in_10(M_10_d_out), .in_11(M_11_d_out), .in_12(M_12_d_out), .in_13(M_13_d_out), .in_14(M_14_d_out),
    .in_15(M_15_d_out), .out(D_out));

  assign A_out = A_In;
endmodule
