// Digital circuit 4bit_Adder-subtractor.dig as structural Verilog
module _4bit_Adder_subtractor (
  input  [3:0] A,
  input  [3:0] B,
  input  C_in,
  output [3:0] Sum,
  output Carry
);

  wire _1bit_full_adder_1_p5, _1bit_full_adder_2_p5, _1bit_full_adder_3_p5, xor_1_out, xor_2_out, xor_3_out,
       xor_4_out;

  xor xor_1 (xor_1_out, B[0], C_in);
  xor xor_2 (xor_2_out, B[1], C_in);
  xor xor_3 (xor_3_out, B[2], C_in);
  xor xor_4 (xor_4_out, B[3], C_in);
  // _1bit_full_adder _1bit_full_adder_1: pin names not known; wires that end beside it: A[0], xor_1_out, C_in, Sum[0], _1bit_full_adder_1_p5
  // _1bit_full_adder _1bit_full_adder_2: pin names not known; wires that end beside it: A[1], xor_2_out, _1bit_full_adder_1_p5, Sum[1], _1bit_full_adder_2_p5
  // _1bit_full_adder _1bit_full_adder_3: pin names not known; wires that end beside it: A[2], xor_3_out, _1bit_full_adder_2_p5, Sum[2], _1bit_full_adder_3_p5
  // _1bit_full_adder _1bit_full_adder_4: pin names not known; wires that end beside it: A[3], xor_4_out, _1bit_full_adder_3_p5, Sum[3], Carry
endmodule
