// Digital circuit 4bit_CPU.dlogic.dig as structural Verilog
module _4bit_CPU_dlogic (
  input  [3:0] Jump,
  input  Load,
  input  Clock,
  input  [3:0] Data,
  output [3:0] out_3,
  output [3:0] out_4,
  output [3:0] out_5,
  output [3:0] out_6,
  output Overflow,
  output Zero,
  output SLT,
  output [3:0] Expected_Result,
  output [3:0] out_11
);

  wire demultiplexer_1_out_0, demultiplexer_1_out_1, not_1_out;
  wire [3:0] demultiplexer_2_out_0, demultiplexer_2_out_1, RAM_a_out, RAM_d_out;

  // PC_register PC: pin names not known; wires that end beside it: Jump, Load, Clock, out_3, out_11
  not not_1 (not_1_out, Load);
  _16x4bit_mem RAM (.Write(not_1_out), .A_In(out_3), .D_in(Data), .D_out(RAM_d_out), .A_out(RAM_a_out));
  Demultiplexer demultiplexer_1 (
    .sel(out_4[3]), .in(1'b1), .out_0(demultiplexer_1_out_0), .out_1(demultiplexer_1_out_1));
  Demultiplexer #(.Bits(4)) demultiplexer_2 (
    .sel(out_4[3]), .in(RAM_d_out), .out_0(demultiplexer_2_out_0), .out_1(demultiplexer_2_out_1));
  // _4bit_register IR: pin names not known; wires that end beside it: RAM_d_out, 1'b1, Clock, out_4
  // _4bit_register A: pin names not known; wires that end beside it: demultiplexer_2_out_0, demultiplexer_1_out_0, Clock, out_5
  // _4bit_register B: pin names not known; wires that end beside it: demultiplexer_2_out_1, demultiplexer_1_out_1, Clock, out_6
  // _4bit_ALU_dlogic ALU: pin names not known; wires that end beside it: out_5, out_6, out_4[2:0], Overflow, Zero, SLT, Expected_Result
endmodule
