// Digital circuit 4bit_incrementor.dig as structural Verilog
module _4bit_incrementor (
  input  [3:0] A,
  output C__out
);

  wire and_2_out, and_3_out, and_4_out, xor_1_out, xor_2_out, xor_3_out, xor_4_out;

  xor xor_1 (xor_1_out, and_2_out, A[3]);
  xor xor_2 (xor_2_out, and_3_out, A[2]);
  xor xor_3 (xor_3_out, and_4_out, A[1]);
  xor xor_4 (xor_4_out, A[0], 1'b1);
  and and_1 (C__out, and_2_out, A[3]);
  and and_2 (and_2_out, and_3_out, A[2]);
  and and_3 (and_3_out, and_4_out, A[1]);
  and and_4 (and_4_out, 1'b1, A[0]);
endmodule
