// Digital circuit 4bit_register.dig as structural Verilog
module _4bit_register (
  input  [3:0] D,
  input  [1:0] Control,
  input  Clock,
  output [3:0] Q
);

  wire [3:0] multiplexer_1_out;

  Multiplexer #(.Bits(4), .Selector_Bits(2)) multiplexer_1 (
    .sel(Control), .in_0(Q), .in_1(D), .in_2(4'b0000), .in_3(4'b0000), .out(multiplexer_1_out));
  D_FF d_ff_1 (.D(multiplexer_1_out[0]), .C(Clock), .Q(Q[0]));  // open: nQ
  D_FF d_ff_2 (.D(multiplexer_1_out[1]), .C(Clock), .Q(Q[1]));  // open: nQ
  D_FF d_ff_3 (.D(multiplexer_1_out[2]), .C(Clock), .Q(Q[2]));  // open: nQ
  D_FF d_ff_4 (.D(multiplexer_1_out[3]), .C(Clock), .Q(Q[3]));  // open: nQ

  // Notes on the sheet:
  //   Clock: Hz: 2147483647
endmodule
