// Digital circuit PC register.dig as structural Verilog
module PC_register (
  input  [3:0] D,
  input  Set,
  input  R,
  input  Clock,
  output [3:0] Q
);

  D_FF_AS d_ff_as_1 (.Set(Set), .D(D[0]), .C(Clock), .Clr(R), .Q(Q[0]));  // open: nQ
  D_FF_AS d_ff_as_2 (.Set(Set), .D(D[1]), .C(Clock), .Clr(R), .Q(Q[1]));  // open: nQ
  D_FF_AS d_ff_as_3 (.Set(Set), .D(D[2]), .C(Clock), .Clr(R), .Q(Q[2]));  // open: nQ
  D_FF_AS d_ff_as_4 (.Set(Set), .D(D[3]), .C(Clock), .Clr(R), .Q(Q[3]));  // open: nQ

  // Notes on the sheet:
  //   Clock: Hz: 2147483647
endmodule
